# Fritzing sketch Joystick_KY-023 (saved by Fritzing 0.9.3b)

parts:
  Part2 = Arduino Sensor Shield v5.0
  Part3 = Arduino Uno (Rev3)  # not connected
  Part4 = Black Joystick KY-023

nets:
  N1: Part2.A0, Part4.VRx
  N2: Part2.A1, Part4.VRy
  N3: Part2.A2, Part4.SW
  GND: Part2.GND, Part4.GND
  +5V: Part2.+5V, Part4.+5V

custom parts:
  Black Joystick KY-023: Description: The joystick is a combination of 2 analoog potentiometer and a digital switch. Arduino GND --> Module pin - Arduino +5V --> Module pin +5V Arduino Analoog 0 --> Module VRx Arduino Analoog 1 --> Module VRy Arduino Digital --> Module SW Dimensions: 1" x 1.25"
