# Fritzing sketch lcd_brazo (saved by Fritzing 0.9.3b)

parts:
  Part1 = Arduino Sensor Shield v5.0
  Part2 = Arduino Uno (Rev3)  # not connected
  Part3 = LCD1602-I2C

nets:
  GND: Part1.GND, Part3.GND
  +5V: Part1.+5V, Part1.SCL, Part3.VCC, Part3.SCL
  N1: Part1.SDA, Part3.SDA

custom parts:
  LCD1602-I2C: A standard character display, usually with 2x16 characters. Comes in many colors with LCM1602 IIC attached.
